// Digital circuit fpga-simulation.dig as structural Verilog
module fpga_simulation (
  input  CLK,
  input  [31:0] W15,
  input  [31:0] W0,
  input  [31:0] W4,
  input  [31:0] W5,
  input  [31:0] W6,
  input  [31:0] W7,
  input  [31:0] W8,
  input  [31:0] W9,
  input  [31:0] W10,
  input  [31:0] W11,
  input  [31:0] W12,
  input  [31:0] W13,
  input  [31:0] W14,
  input  [31:0] W3,
  input  [31:0] W2,
  input  [31:0] W1,
  output [31:0] a,
  output [31:0] b,
  output [31:0] c,
  output [31:0] d,
  output [31:0] e,
  output [31:0] f,
  output [31:0] g,
  output [31:0] h
);

  wire comparator_1_eq, rs_ff_as_1_q;
  wire [4:0] counter_1_out;
  wire [5:0] add_1_s, add_2_s, add_3_s;
  wire [9:0] mul_1_mul;
  wire [31:0] add_4_s, add_5_s, add_6_s, add_7_s, add_8_s, add_9_s, add_10_s, add_11_s, add_12_s, add_13_s,
       add_14_s, add_15_s, add_28_s, add_29_s, add_30_s, add_31_s, add_38_s, add_39_s, add_40_s, add_41_s,
       and_1_out, and_2_out, and_3_out, and_4_out, and_5_out, and_6_out, and_7_out, and_8_out, and_9_out,
       and_10_out, and_11_out, and_12_out, and_13_out, and_14_out, and_15_out, and_16_out, and_17_out,
       and_18_out, and_19_out, and_20_out, barrelshifter_1_out, barrelshifter_2_out, barrelshifter_3_out,
       barrelshifter_4_out, barrelshifter_5_out, barrelshifter_6_out, barrelshifter_7_out,
       barrelshifter_8_out, barrelshifter_9_out, barrelshifter_10_out, barrelshifter_11_out,
       barrelshifter_12_out, barrelshifter_13_out, barrelshifter_14_out, barrelshifter_15_out,
       barrelshifter_16_out, barrelshifter_17_out, barrelshifter_18_out, barrelshifter_19_out,
       barrelshifter_20_out, barrelshifter_21_out, barrelshifter_22_out, barrelshifter_23_out,
       barrelshifter_24_out, barrelshifter_25_out, barrelshifter_26_out, barrelshifter_27_out,
       barrelshifter_28_out, barrelshifter_29_out, barrelshifter_30_out, barrelshifter_31_out,
       barrelshifter_32_out, barrelshifter_33_out, barrelshifter_34_out, barrelshifter_35_out,
       barrelshifter_36_out, barrelshifter_37_out, barrelshifter_38_out, barrelshifter_39_out,
       barrelshifter_40_out, barrelshifter_41_out, barrelshifter_42_out, barrelshifter_43_out,
       barrelshifter_44_out, barrelshifter_45_out, barrelshifter_46_out, barrelshifter_47_out,
       barrelshifter_48_out, K0, K1, K2, K3, next_a0, next_a1, next_a2, next_a3, next_e0, next_e1, next_e2,
       next_e3, next_W0, next_W1, next_W2, next_W3, S00, S01, S02, S03, S10, S11, S12, S13, T10, T11, T12,
       T13, T20, T21, T22, T23, W0_q, W0_t, W1_q, W1_t, W2_q, W2_t, W3_q, W3_t, W4_q, W4_t, W5_q, W5_t, W6_q,
       W6_t, W7_q, W7_t, W8_q, W8_t, W9_q, W9_t, W10_q, W10_t, W11_q, W11_t, W12_q, W12_t, W13_q, W13_t,
       W14_q, W14_t, W15_q, W15_t, xor_1_out, xor_2_out, xor_3_out, xor_4_out, xor_5_out, xor_6_out,
       xor_7_out, xor_8_out, xor_9_out, xor_10_out, xor_11_out, xor_12_out, xor_13_out, xor_14_out,
       xor_15_out, xor_16_out, xor_17_out, xor_18_out, xor_19_out, xor_20_out, xor_21_out, xor_22_out,
       xor_23_out, xor_24_out, xor_25_out, xor_26_out, xor_27_out, xor_28_out, xor_29_out, xor_30_out,
       xor_31_out, xor_32_out, xor_37_out, xor_38_out, xor_39_out, xor_40_out;

  BarrelShifter #(.Bits(32), .barrelShifterMode("rotate"), .direction("right")) barrelshifter_1 (
    .in(e), .shift(6'b000110), .out(barrelshifter_1_out));
  BarrelShifter #(.Bits(32), .barrelShifterMode("rotate"), .direction("right")) barrelshifter_2 (
    .in(e), .shift(6'b001011), .out(barrelshifter_2_out));
  BarrelShifter #(.Bits(32), .barrelShifterMode("rotate"), .direction("right")) barrelshifter_3 (
    .in(next_e0), .shift(6'b000110), .out(barrelshifter_3_out));
  BarrelShifter #(.Bits(32), .barrelShifterMode("rotate"), .direction("right")) barrelshifter_4 (
    .in(next_e0), .shift(6'b001011), .out(barrelshifter_4_out));
  BarrelShifter #(.Bits(32), .barrelShifterMode("rotate"), .direction("right")) barrelshifter_5 (
    .in(next_e1), .shift(6'b000110), .out(barrelshifter_5_out));
  BarrelShifter #(.Bits(32), .barrelShifterMode("rotate"), .direction("right")) barrelshifter_6 (
    .in(next_e1), .shift(6'b001011), .out(barrelshifter_6_out));
  BarrelShifter #(.Bits(32), .barrelShifterMode("rotate"), .direction("right")) barrelshifter_7 (
    .in(next_e2), .shift(6'b000110), .out(barrelshifter_7_out));
  BarrelShifter #(.Bits(32), .barrelShifterMode("rotate"), .direction("right")) barrelshifter_8 (
    .in(next_e2), .shift(6'b001011), .out(barrelshifter_8_out));
  D_FF #(.Bits(32)) u_W15 (.D(next_W3), .C(CLK), .Q(W15_q));  // open: nQ
  D_FF #(.Bits(32)) u_W14 (.D(next_W2), .C(CLK), .Q(W14_q));  // open: nQ
  D_FF #(.Bits(32)) u_W13 (.D(next_W1), .C(CLK), .Q(W13_q));  // open: nQ
  D_FF #(.Bits(32)) u_W12 (.D(next_W0), .C(CLK), .Q(W12_q));  // open: nQ
  Counter #(.Bits(5)) counter_1 (.en(1'b1), .C(CLK), .clr(1'b0), .out(counter_1_out));  // open: ovf
  RS_FF_AS rs_ff_as_1 (.S(CLK), .R(1'b0), .Q(rs_ff_as_1_q));  // open: nQ
  Multiplexer #(.Bits(32)) multiplexer_1 (.sel(rs_ff_as_1_q), .in_0(W15), .in_1(W15_q), .out(W15_t));
  Multiplexer #(.Bits(32)) multiplexer_2 (.sel(rs_ff_as_1_q), .in_0(W14), .in_1(W14_q), .out(W14_t));
  Multiplexer #(.Bits(32)) multiplexer_3 (.sel(rs_ff_as_1_q), .in_0(W13), .in_1(W13_q), .out(W13_t));
  Multiplexer #(.Bits(32)) multiplexer_4 (.sel(rs_ff_as_1_q), .in_0(W12), .in_1(W12_q), .out(W12_t));
  assign xor_1_out = barrelshifter_1_out ^ barrelshifter_2_out;  // XOr xor_1, 32 bits wide
  BarrelShifter #(.Bits(32), .barrelShifterMode("rotate"), .direction("right")) barrelshifter_9 (
    .in(e), .shift(6'b011001), .out(barrelshifter_9_out));
  assign and_1_out = e & f;  // And and_1, 32 bits wide
  assign and_2_out = ~e & g;  // And and_2, 32 bits wide
  assign xor_2_out = barrelshifter_3_out ^ barrelshifter_4_out;  // XOr xor_2, 32 bits wide
  BarrelShifter #(.Bits(32), .barrelShifterMode("rotate"), .direction("right")) barrelshifter_10 (
    .in(next_e0), .shift(6'b011001), .out(barrelshifter_10_out));
  assign and_3_out = next_e0 & e;  // And and_3, 32 bits wide
  assign and_4_out = ~next_e0 & f;  // And and_4, 32 bits wide
  assign xor_3_out = barrelshifter_5_out ^ barrelshifter_6_out;  // XOr xor_3, 32 bits wide
  BarrelShifter #(.Bits(32), .barrelShifterMode("rotate"), .direction("right")) barrelshifter_11 (
    .in(next_e1), .shift(6'b011001), .out(barrelshifter_11_out));
  assign and_5_out = next_e1 & next_e0;  // And and_5, 32 bits wide
  assign and_6_out = ~next_e1 & e;  // And and_6, 32 bits wide
  assign xor_4_out = barrelshifter_7_out ^ barrelshifter_8_out;  // XOr xor_4, 32 bits wide
  BarrelShifter #(.Bits(32), .barrelShifterMode("rotate"), .direction("right")) barrelshifter_12 (
    .in(next_e2), .shift(6'b011001), .out(barrelshifter_12_out));
  assign and_7_out = next_e2 & next_e1;  // And and_7, 32 bits wide
  assign and_8_out = ~next_e2 & next_e0;  // And and_8, 32 bits wide
  Mul #(.Bits(5)) mul_1 (.a(5'b00100), .b(counter_1_out), .mul(mul_1_mul));
  Comparator #(.Bits(5)) comparator_1 (.a(counter_1_out), .b(5'b10000), .eq(comparator_1_eq));  // open: gt, lt
  Break Done (.brk(comparator_1_eq));
  D_FF #(.Bits(32)) u_W11 (.D(W15_t), .C(CLK), .Q(W11_q));  // open: nQ
  D_FF #(.Bits(32)) u_W10 (.D(W14_t), .C(CLK), .Q(W10_q));  // open: nQ
  D_FF #(.Bits(32)) u_W9 (.D(W13_t), .C(CLK), .Q(W9_q));  // open: nQ
  D_FF #(.Bits(32)) u_W8 (.D(W12_t), .C(CLK), .Q(W8_q));  // open: nQ
  assign xor_5_out = xor_1_out ^ barrelshifter_9_out;  // XOr xor_5, 32 bits wide
  assign xor_6_out = and_1_out ^ and_2_out;  // XOr xor_6, 32 bits wide
  assign xor_7_out = xor_2_out ^ barrelshifter_10_out;  // XOr xor_7, 32 bits wide
  assign xor_8_out = and_3_out ^ and_4_out;  // XOr xor_8, 32 bits wide
  assign xor_9_out = xor_3_out ^ barrelshifter_11_out;  // XOr xor_9, 32 bits wide
  assign xor_10_out = and_5_out ^ and_6_out;  // XOr xor_10, 32 bits wide
  assign xor_11_out = xor_4_out ^ barrelshifter_12_out;  // XOr xor_11, 32 bits wide
  assign xor_12_out = and_7_out ^ and_8_out;  // XOr xor_12, 32 bits wide
  Multiplexer #(.Bits(32)) multiplexer_5 (.sel(rs_ff_as_1_q), .in_0(W11), .in_1(W11_q), .out(W11_t));
  Multiplexer #(.Bits(32)) multiplexer_6 (.sel(rs_ff_as_1_q), .in_0(W10), .in_1(W10_q), .out(W10_t));
  Multiplexer #(.Bits(32)) multiplexer_7 (.sel(rs_ff_as_1_q), .in_0(W9), .in_1(W9_q), .out(W9_t));
  Multiplexer #(.Bits(32)) multiplexer_8 (.sel(rs_ff_as_1_q), .in_0(W8), .in_1(W8_q), .out(W8_t));
  Add #(.Bits(6)) add_1 (.a(mul_1_mul[5:0]), .b(6'b000001), .c_i(1'b0), .s(add_1_s));  // open: c_o
  Add #(.Bits(6)) add_2 (.a(mul_1_mul[5:0]), .b(6'b000010), .c_i(1'b0), .s(add_2_s));  // open: c_o
  Add #(.Bits(6)) add_3 (.a(mul_1_mul[5:0]), .b(6'b000011), .c_i(1'b0), .s(add_3_s));  // open: c_o
  D_FF #(.Bits(32)) u_W7 (.D(W11_t), .C(CLK), .Q(W7_q));  // open: nQ
  D_FF #(.Bits(32)) u_W6 (.D(W10_t), .C(CLK), .Q(W6_q));  // open: nQ
  D_FF #(.Bits(32)) u_W5 (.D(W9_t), .C(CLK), .Q(W5_q));  // open: nQ
  D_FF #(.Bits(32)) u_W4 (.D(W8_t), .C(CLK), .Q(W4_q));  // open: nQ
  Add #(.Bits(32)) add_4 (.a(xor_5_out), .b(xor_6_out), .c_i(1'b0), .s(add_4_s));  // open: c_o
  Add #(.Bits(32)) add_5 (.a(xor_7_out), .b(xor_8_out), .c_i(1'b0), .s(add_5_s));  // open: c_o
  Add #(.Bits(32)) add_6 (.a(xor_9_out), .b(xor_10_out), .c_i(1'b0), .s(add_6_s));  // open: c_o
  Add #(.Bits(32)) add_7 (.a(xor_11_out), .b(xor_12_out), .c_i(1'b0), .s(add_7_s));  // open: c_o
  Multiplexer #(.Bits(32)) multiplexer_9 (.sel(rs_ff_as_1_q), .in_0(W7), .in_1(W7_q), .out(W7_t));
  Multiplexer #(.Bits(32)) multiplexer_10 (.sel(rs_ff_as_1_q), .in_0(W6), .in_1(W6_q), .out(W6_t));
  Multiplexer #(.Bits(32)) multiplexer_11 (.sel(rs_ff_as_1_q), .in_0(W5), .in_1(W5_q), .out(W5_t));
  Multiplexer #(.Bits(32)) multiplexer_12 (.sel(rs_ff_as_1_q), .in_0(W4), .in_1(W4_q), .out(W4_t));
  ROM #(.AddrBits(6), .Bits(32)) K (.A(mul_1_mul[5:0]), .sel(1'b1), .D(K0));
  ROM #(.AddrBits(6), .Bits(32)) K_2 (.A(add_1_s), .sel(1'b1), .D(K1));
  ROM #(.AddrBits(6), .Bits(32)) K_3 (.A(add_2_s), .sel(1'b1), .D(K2));
  ROM #(.AddrBits(6), .Bits(32)) K_4 (.A(add_3_s), .sel(1'b1), .D(K3));
  Add #(.Bits(32)) add_8 (.a(add_4_s), .b(h), .c_i(1'b0), .s(add_8_s));  // open: c_o
  Add #(.Bits(32)) add_9 (.a(add_5_s), .b(g), .c_i(1'b0), .s(add_9_s));  // open: c_o
  Add #(.Bits(32)) add_10 (.a(add_6_s), .b(f), .c_i(1'b0), .s(add_10_s));  // open: c_o
  Add #(.Bits(32)) add_11 (.a(add_7_s), .b(e), .c_i(1'b0), .s(add_11_s));  // open: c_o
  D_FF #(.Bits(32)) u_W3 (.D(W7_t), .C(CLK), .Q(W3_q));  // open: nQ
  D_FF #(.Bits(32)) u_W2 (.D(W6_t), .C(CLK), .Q(W2_q));  // open: nQ
  D_FF #(.Bits(32)) u_W1 (.D(W5_t), .C(CLK), .Q(W1_q));  // open: nQ
  D_FF #(.Bits(32)) u_W0 (.D(W4_t), .C(CLK), .Q(W0_q));  // open: nQ
  Add #(.Bits(32)) add_12 (.a(K0), .b(W0_t), .c_i(1'b0), .s(add_12_s));  // open: c_o
  Add #(.Bits(32)) add_13 (.a(K1), .b(W1_t), .c_i(1'b0), .s(add_13_s));  // open: c_o
  Add #(.Bits(32)) add_14 (.a(K2), .b(W2_t), .c_i(1'b0), .s(add_14_s));  // open: c_o
  Add #(.Bits(32)) add_15 (.a(K3), .b(W3_t), .c_i(1'b0), .s(add_15_s));  // open: c_o
  Multiplexer #(.Bits(32)) multiplexer_13 (.sel(rs_ff_as_1_q), .in_0(W3), .in_1(W3_q), .out(W3_t));
  Multiplexer #(.Bits(32)) multiplexer_14 (.sel(rs_ff_as_1_q), .in_0(W2), .in_1(W2_q), .out(W2_t));
  Multiplexer #(.Bits(32)) multiplexer_15 (.sel(rs_ff_as_1_q), .in_0(W1), .in_1(W1_q), .out(W1_t));
  Multiplexer #(.Bits(32)) multiplexer_16 (.sel(rs_ff_as_1_q), .in_0(W0), .in_1(W0_q), .out(W0_t));
  Add #(.Bits(32)) add_16 (.a(add_12_s), .b(add_8_s), .c_i(1'b0), .s(T10));  // open: c_o
  Add #(.Bits(32)) add_17 (.a(add_13_s), .b(add_9_s), .c_i(1'b0), .s(T11));  // open: c_o
  Add #(.Bits(32)) add_18 (.a(add_14_s), .b(add_10_s), .c_i(1'b0), .s(T12));  // open: c_o
  Add #(.Bits(32)) add_19 (.a(add_15_s), .b(add_11_s), .c_i(1'b0), .s(T13));  // open: c_o
  Add #(.Bits(32)) add_20 (.a(d), .b(T10), .c_i(1'b0), .s(next_e0));  // open: c_o
  Add #(.Bits(32)) add_21 (.a(c), .b(T11), .c_i(1'b0), .s(next_e1));  // open: c_o
  Add #(.Bits(32)) add_22 (.a(b), .b(T12), .c_i(1'b0), .s(next_e2));  // open: c_o
  Add #(.Bits(32)) add_23 (.a(a), .b(T13), .c_i(1'b0), .s(next_e3));  // open: c_o
  BarrelShifter #(.Bits(32), .barrelShifterMode("rotate"), .direction("right")) barrelshifter_13 (
    .in(a), .shift(6'b000010), .out(barrelshifter_13_out));
  BarrelShifter #(.Bits(32), .barrelShifterMode("rotate"), .direction("right")) barrelshifter_14 (
    .in(a), .shift(6'b001101), .out(barrelshifter_14_out));
  BarrelShifter #(.Bits(32), .barrelShifterMode("rotate"), .direction("right")) barrelshifter_15 (
    .in(next_a0), .shift(6'b000010), .out(barrelshifter_15_out));
  BarrelShifter #(.Bits(32), .barrelShifterMode("rotate"), .direction("right")) barrelshifter_16 (
    .in(next_a0), .shift(6'b001101), .out(barrelshifter_16_out));
  BarrelShifter #(.Bits(32), .barrelShifterMode("rotate"), .direction("right")) barrelshifter_17 (
    .in(next_a1), .shift(6'b000010), .out(barrelshifter_17_out));
  BarrelShifter #(.Bits(32), .barrelShifterMode("rotate"), .direction("right")) barrelshifter_18 (
    .in(next_a1), .shift(6'b001101), .out(barrelshifter_18_out));
  BarrelShifter #(.Bits(32), .barrelShifterMode("rotate"), .direction("right")) barrelshifter_19 (
    .in(next_a2), .shift(6'b000010), .out(barrelshifter_19_out));
  BarrelShifter #(.Bits(32), .barrelShifterMode("rotate"), .direction("right")) barrelshifter_20 (
    .in(next_a2), .shift(6'b001101), .out(barrelshifter_20_out));
  D_FF #(.Bits(32), .Default(1779033703)) u_A (.D(next_a3), .C(CLK), .Q(a));  // open: nQ
  D_FF #(.Bits(32), .Default(3144134277)) u_B (.D(next_a2), .C(CLK), .Q(b));  // open: nQ
  D_FF #(.Bits(32), .Default(1013904242)) u_C (.D(next_a1), .C(CLK), .Q(c));  // open: nQ
  D_FF #(.Bits(32), .Default(2773480762)) u_D (.D(next_a0), .C(CLK), .Q(d));  // open: nQ
  D_FF #(.Bits(32), .Default(1359893119)) u_E (.D(next_e3), .C(CLK), .Q(e));  // open: nQ
  D_FF #(.Bits(32), .Default(2600822924)) u_F (.D(next_e2), .C(CLK), .Q(f));  // open: nQ
  D_FF #(.Bits(32), .Default(528734635)) u_G (.D(next_e1), .C(CLK), .Q(g));  // open: nQ
  D_FF #(.Bits(32), .Default(1541459225)) u_H (.D(next_e0), .C(CLK), .Q(h));  // open: nQ
  Add #(.Bits(32)) add_24 (.a(T20), .b(T10), .c_i(1'b0), .s(next_a0));  // open: c_o
  Add #(.Bits(32)) add_25 (.a(T21), .b(T11), .c_i(1'b0), .s(next_a1));  // open: c_o
  Add #(.Bits(32)) add_26 (.a(T22), .b(T12), .c_i(1'b0), .s(next_a2));  // open: c_o
  Add #(.Bits(32)) add_27 (.a(T23), .b(T13), .c_i(1'b0), .s(next_a3));  // open: c_o
  assign xor_13_out = barrelshifter_13_out ^ barrelshifter_14_out;  // XOr xor_13, 32 bits wide
  BarrelShifter #(.Bits(32), .barrelShifterMode("rotate"), .direction("right")) barrelshifter_21 (
    .in(a), .shift(6'b010110), .out(barrelshifter_21_out));
  assign and_9_out = a & b;  // And and_9, 32 bits wide
  assign and_10_out = a & c;  // And and_10, 32 bits wide
  assign xor_14_out = barrelshifter_15_out ^ barrelshifter_16_out;  // XOr xor_14, 32 bits wide
  BarrelShifter #(.Bits(32), .barrelShifterMode("rotate"), .direction("right")) barrelshifter_22 (
    .in(next_a0), .shift(6'b010110), .out(barrelshifter_22_out));
  assign and_11_out = next_a0 & a;  // And and_11, 32 bits wide
  assign and_12_out = next_a0 & b;  // And and_12, 32 bits wide
  assign xor_15_out = barrelshifter_17_out ^ barrelshifter_18_out;  // XOr xor_15, 32 bits wide
  BarrelShifter #(.Bits(32), .barrelShifterMode("rotate"), .direction("right")) barrelshifter_23 (
    .in(next_a1), .shift(6'b010110), .out(barrelshifter_23_out));
  assign and_13_out = next_a1 & next_a0;  // And and_13, 32 bits wide
  assign and_14_out = next_a1 & a;  // And and_14, 32 bits wide
  assign xor_16_out = barrelshifter_19_out ^ barrelshifter_20_out;  // XOr xor_16, 32 bits wide
  BarrelShifter #(.Bits(32), .barrelShifterMode("rotate"), .direction("right")) barrelshifter_24 (
    .in(next_a2), .shift(6'b010110), .out(barrelshifter_24_out));
  assign and_15_out = next_a2 & next_a1;  // And and_15, 32 bits wide
  assign and_16_out = next_a2 & next_a0;  // And and_16, 32 bits wide
  assign xor_17_out = xor_13_out ^ barrelshifter_21_out;  // XOr xor_17, 32 bits wide
  assign xor_18_out = and_9_out ^ and_10_out;  // XOr xor_18, 32 bits wide
  assign and_17_out = c & b;  // And and_17, 32 bits wide
  assign xor_19_out = xor_14_out ^ barrelshifter_22_out;  // XOr xor_19, 32 bits wide
  assign xor_20_out = and_11_out ^ and_12_out;  // XOr xor_20, 32 bits wide
  assign and_18_out = b & a;  // And and_18, 32 bits wide
  assign xor_21_out = xor_15_out ^ barrelshifter_23_out;  // XOr xor_21, 32 bits wide
  assign xor_22_out = and_13_out ^ and_14_out;  // XOr xor_22, 32 bits wide
  assign and_19_out = a & next_a0;  // And and_19, 32 bits wide
  assign xor_23_out = xor_16_out ^ barrelshifter_24_out;  // XOr xor_23, 32 bits wide
  assign xor_24_out = and_15_out ^ and_16_out;  // XOr xor_24, 32 bits wide
  assign and_20_out = next_a0 & next_a1;  // And and_20, 32 bits wide
  BarrelShifter #(.Bits(32), .barrelShifterMode("rotate"), .direction("right")) barrelshifter_25 (
    .in(W1_t), .shift(6'b000111), .out(barrelshifter_25_out));
  BarrelShifter #(.Bits(32), .barrelShifterMode("rotate"), .direction("right")) barrelshifter_26 (
    .in(W1_t), .shift(6'b010010), .out(barrelshifter_26_out));
  BarrelShifter #(.Bits(32), .barrelShifterMode("rotate"), .direction("right")) barrelshifter_27 (
    .in(W2_t), .shift(6'b000111), .out(barrelshifter_27_out));
  BarrelShifter #(.Bits(32), .barrelShifterMode("rotate"), .direction("right")) barrelshifter_28 (
    .in(W2_t), .shift(6'b010010), .out(barrelshifter_28_out));
  BarrelShifter #(.Bits(32), .barrelShifterMode("rotate"), .direction("right")) barrelshifter_29 (
    .in(W3_t), .shift(6'b000111), .out(barrelshifter_29_out));
  BarrelShifter #(.Bits(32), .barrelShifterMode("rotate"), .direction("right")) barrelshifter_30 (
    .in(W3_t), .shift(6'b010010), .out(barrelshifter_30_out));
  BarrelShifter #(.Bits(32), .barrelShifterMode("rotate"), .direction("right")) barrelshifter_31 (
    .in(W4_t), .shift(6'b000111), .out(barrelshifter_31_out));
  BarrelShifter #(.Bits(32), .barrelShifterMode("rotate"), .direction("right")) barrelshifter_32 (
    .in(W4_t), .shift(6'b010010), .out(barrelshifter_32_out));
  assign xor_25_out = xor_18_out ^ and_17_out;  // XOr xor_25, 32 bits wide
  assign xor_26_out = xor_20_out ^ and_18_out;  // XOr xor_26, 32 bits wide
  assign xor_27_out = xor_22_out ^ and_19_out;  // XOr xor_27, 32 bits wide
  assign xor_28_out = xor_24_out ^ and_20_out;  // XOr xor_28, 32 bits wide
  Add #(.Bits(32)) add_28 (.a(W0_t), .b(S00), .c_i(1'b0), .s(add_28_s));  // open: c_o
  Add #(.Bits(32)) add_29 (.a(W9_t), .b(S10), .c_i(1'b0), .s(add_29_s));  // open: c_o
  Add #(.Bits(32)) add_30 (.a(W2_t), .b(S02), .c_i(1'b0), .s(add_30_s));  // open: c_o
  Add #(.Bits(32)) add_31 (.a(W11_t), .b(S12), .c_i(1'b0), .s(add_31_s));  // open: c_o
  assign xor_29_out = barrelshifter_25_out ^ barrelshifter_26_out;  // XOr xor_29, 32 bits wide
  BarrelShifter #(.Bits(32), .direction("right")) barrelshifter_33 (
    .in(W1_t), .shift(6'b000011), .out(barrelshifter_33_out));
  assign xor_30_out = barrelshifter_27_out ^ barrelshifter_28_out;  // XOr xor_30, 32 bits wide
  BarrelShifter #(.Bits(32), .direction("right")) barrelshifter_34 (
    .in(W2_t), .shift(6'b000011), .out(barrelshifter_34_out));
  assign xor_31_out = barrelshifter_29_out ^ barrelshifter_30_out;  // XOr xor_31, 32 bits wide
  BarrelShifter #(.Bits(32), .direction("right")) barrelshifter_35 (
    .in(W3_t), .shift(6'b000011), .out(barrelshifter_35_out));
  assign xor_32_out = barrelshifter_31_out ^ barrelshifter_32_out;  // XOr xor_32, 32 bits wide
  BarrelShifter #(.Bits(32), .direction("right")) barrelshifter_36 (
    .in(W4_t), .shift(6'b000011), .out(barrelshifter_36_out));
  Add #(.Bits(32)) add_32 (.a(xor_17_out), .b(xor_25_out), .c_i(1'b0), .s(T20));  // open: c_o
  Add #(.Bits(32)) add_33 (.a(xor_19_out), .b(xor_26_out), .c_i(1'b0), .s(T21));  // open: c_o
  Add #(.Bits(32)) add_34 (.a(xor_21_out), .b(xor_27_out), .c_i(1'b0), .s(T22));  // open: c_o
  Add #(.Bits(32)) add_35 (.a(xor_23_out), .b(xor_28_out), .c_i(1'b0), .s(T23));  // open: c_o
  Add #(.Bits(32)) add_36 (.a(add_28_s), .b(add_29_s), .c_i(1'b0), .s(next_W0));  // open: c_o
  Add #(.Bits(32)) add_37 (.a(add_30_s), .b(add_31_s), .c_i(1'b0), .s(next_W2));  // open: c_o
  assign S00 = xor_29_out ^ barrelshifter_33_out;  // XOr xor_33, 32 bits wide
  assign S01 = xor_30_out ^ barrelshifter_34_out;  // XOr xor_34, 32 bits wide
  assign S02 = xor_31_out ^ barrelshifter_35_out;  // XOr xor_35, 32 bits wide
  assign S03 = xor_32_out ^ barrelshifter_36_out;  // XOr xor_36, 32 bits wide
  BarrelShifter #(.Bits(32), .barrelShifterMode("rotate"), .direction("right")) barrelshifter_37 (
    .in(W14_t), .shift(6'b010001), .out(barrelshifter_37_out));
  BarrelShifter #(.Bits(32), .barrelShifterMode("rotate"), .direction("right")) barrelshifter_38 (
    .in(W14_t), .shift(6'b010011), .out(barrelshifter_38_out));
  BarrelShifter #(.Bits(32), .barrelShifterMode("rotate"), .direction("right")) barrelshifter_39 (
    .in(W15_t), .shift(6'b010001), .out(barrelshifter_39_out));
  BarrelShifter #(.Bits(32), .barrelShifterMode("rotate"), .direction("right")) barrelshifter_40 (
    .in(W15_t), .shift(6'b010011), .out(barrelshifter_40_out));
  BarrelShifter #(.Bits(32), .barrelShifterMode("rotate"), .direction("right")) barrelshifter_41 (
    .in(next_W0), .shift(6'b010001), .out(barrelshifter_41_out));
  BarrelShifter #(.Bits(32), .barrelShifterMode("rotate"), .direction("right")) barrelshifter_42 (
    .in(next_W0), .shift(6'b010011), .out(barrelshifter_42_out));
  BarrelShifter #(.Bits(32), .barrelShifterMode("rotate"), .direction("right")) barrelshifter_43 (
    .in(next_W1), .shift(6'b010001), .out(barrelshifter_43_out));
  BarrelShifter #(.Bits(32), .barrelShifterMode("rotate"), .direction("right")) barrelshifter_44 (
    .in(next_W1), .shift(6'b010011), .out(barrelshifter_44_out));
  assign xor_37_out = barrelshifter_37_out ^ barrelshifter_38_out;  // XOr xor_37, 32 bits wide
  BarrelShifter #(.Bits(32), .direction("right")) barrelshifter_45 (
    .in(W14_t), .shift(6'b001010), .out(barrelshifter_45_out));
  assign xor_38_out = barrelshifter_39_out ^ barrelshifter_40_out;  // XOr xor_38, 32 bits wide
  BarrelShifter #(.Bits(32), .direction("right")) barrelshifter_46 (
    .in(W15_t), .shift(6'b001010), .out(barrelshifter_46_out));
  assign xor_39_out = barrelshifter_41_out ^ barrelshifter_42_out;  // XOr xor_39, 32 bits wide
  BarrelShifter #(.Bits(32), .direction("right")) barrelshifter_47 (
    .in(next_W0), .shift(6'b001010), .out(barrelshifter_47_out));
  assign xor_40_out = barrelshifter_43_out ^ barrelshifter_44_out;  // XOr xor_40, 32 bits wide
  BarrelShifter #(.Bits(32), .direction("right")) barrelshifter_48 (
    .in(next_W1), .shift(6'b001010), .out(barrelshifter_48_out));
  Add #(.Bits(32)) add_38 (.a(W1_t), .b(S01), .c_i(1'b0), .s(add_38_s));  // open: c_o
  Add #(.Bits(32)) add_39 (.a(W10_t), .b(S11), .c_i(1'b0), .s(add_39_s));  // open: c_o
  Add #(.Bits(32)) add_40 (.a(W3_t), .b(S03), .c_i(1'b0), .s(add_40_s));  // open: c_o
  Add #(.Bits(32)) add_41 (.a(W12_t), .b(S13), .c_i(1'b0), .s(add_41_s));  // open: c_o
  assign S10 = xor_37_out ^ barrelshifter_45_out;  // XOr xor_41, 32 bits wide
  assign S11 = xor_38_out ^ barrelshifter_46_out;  // XOr xor_42, 32 bits wide
  assign S12 = xor_39_out ^ barrelshifter_47_out;  // XOr xor_43, 32 bits wide
  assign S13 = xor_40_out ^ barrelshifter_48_out;  // XOr xor_44, 32 bits wide
  Add #(.Bits(32)) add_42 (.a(add_38_s), .b(add_39_s), .c_i(1'b0), .s(next_W1));  // open: c_o
  Add #(.Bits(32)) add_43 (.a(add_40_s), .b(add_41_s), .c_i(1'b0), .s(next_W3));  // open: c_o

  // Notes on the sheet:
  //   CLK: Hz: 2
  //   contents of K (hex, n*v repeats v):
  //   428a2f98,71374491,b5c0fbcf,e9b5dba5,3956c25b,59f111f1,923f82a4
  //   ,ab1c5ed5,d807aa98,12835b01,243185be,550c7dc3,72be5d74,80deb1fe
  //   ,9bdc06a7,c19bf174,e49b69c1,efbe4786,fc19dc6,240ca1cc,2de92c6f
  //   ,4a7484aa,5cb0a9dc,76f988da,983e5152,a831c66d,b00327c8,bf597fc7
  //   ,c6e00bf3,d5a79147,6ca6351,14292967,27b70a85,2e1b2138,4d2c6dfc
  //   ,53380d13,650a7354,766a0abb,81c2c92e,92722c85,a2bfe8a1,a81a664b
  //   ,c24b8b70,c76c51a3,d192e819,d6990624,f40e3585,106aa070,19a4c116
  //   ,1e376c08,2748774c,34b0bcb5,391c0cb3,4ed8aa4a,5b9cca4f,682e6ff3
  //   ,748f82ee,78a5636f,84c87814,8cc70208,90befffa,a4506ceb,bef9a3f7,c67178f2
  //   contents of K_2 (hex, n*v repeats v):
  //   428a2f98,71374491,b5c0fbcf,e9b5dba5,3956c25b,59f111f1,923f82a4
  //   ,ab1c5ed5,d807aa98,12835b01,243185be,550c7dc3,72be5d74,80deb1fe
  //   ,9bdc06a7,c19bf174,e49b69c1,efbe4786,fc19dc6,240ca1cc,2de92c6f
  //   ,4a7484aa,5cb0a9dc,76f988da,983e5152,a831c66d,b00327c8,bf597fc7
  //   ,c6e00bf3,d5a79147,6ca6351,14292967,27b70a85,2e1b2138,4d2c6dfc
  //   ,53380d13,650a7354,766a0abb,81c2c92e,92722c85,a2bfe8a1,a81a664b
  //   ,c24b8b70,c76c51a3,d192e819,d6990624,f40e3585,106aa070,19a4c116
  //   ,1e376c08,2748774c,34b0bcb5,391c0cb3,4ed8aa4a,5b9cca4f,682e6ff3
  //   ,748f82ee,78a5636f,84c87814,8cc70208,90befffa,a4506ceb,bef9a3f7,c67178f2
  //   contents of K_3 (hex, n*v repeats v):
  //   428a2f98,71374491,b5c0fbcf,e9b5dba5,3956c25b,59f111f1,923f82a4
  //   ,ab1c5ed5,d807aa98,12835b01,243185be,550c7dc3,72be5d74,80deb1fe
  //   ,9bdc06a7,c19bf174,e49b69c1,efbe4786,fc19dc6,240ca1cc,2de92c6f
  //   ,4a7484aa,5cb0a9dc,76f988da,983e5152,a831c66d,b00327c8,bf597fc7
  //   ,c6e00bf3,d5a79147,6ca6351,14292967,27b70a85,2e1b2138,4d2c6dfc
  //   ,53380d13,650a7354,766a0abb,81c2c92e,92722c85,a2bfe8a1,a81a664b
  //   ,c24b8b70,c76c51a3,d192e819,d6990624,f40e3585,106aa070,19a4c116
  //   ,1e376c08,2748774c,34b0bcb5,391c0cb3,4ed8aa4a,5b9cca4f,682e6ff3
  //   ,748f82ee,78a5636f,84c87814,8cc70208,90befffa,a4506ceb,bef9a3f7,c67178f2
  //   contents of K_4 (hex, n*v repeats v):
  //   428a2f98,71374491,b5c0fbcf,e9b5dba5,3956c25b,59f111f1,923f82a4
  //   ,ab1c5ed5,d807aa98,12835b01,243185be,550c7dc3,72be5d74,80deb1fe
  //   ,9bdc06a7,c19bf174,e49b69c1,efbe4786,fc19dc6,240ca1cc,2de92c6f
  //   ,4a7484aa,5cb0a9dc,76f988da,983e5152,a831c66d,b00327c8,bf597fc7
  //   ,c6e00bf3,d5a79147,6ca6351,14292967,27b70a85,2e1b2138,4d2c6dfc
  //   ,53380d13,650a7354,766a0abb,81c2c92e,92722c85,a2bfe8a1,a81a664b
  //   ,c24b8b70,c76c51a3,d192e819,d6990624,f40e3585,106aa070,19a4c116
  //   ,1e376c08,2748774c,34b0bcb5,391c0cb3,4ed8aa4a,5b9cca4f,682e6ff3
  //   ,748f82ee,78a5636f,84c87814,8cc70208,90befffa,a4506ceb,bef9a3f7,c67178f2
endmodule
